# Fritzing sketch Pi_Schematic (saved by Fritzing 0.9.3b)
breadboards: 1

parts:
  Raspberry_Pi_1 = Raspberry Pi 3 [part_number=RPI-3-V1.2]
  LED1 = LED - 3mm [color="Red (633nm)" package="3 mm [THT]"]
  U3 = HALL-EFFECT [package=sc70]
  R1 = Resistor [tolerance=±5% resistance=10k package=THT]
  U1 = ID-12_20 [package=id-12]
  LED3 = LED - 3mm [color="Green (570nm)" package="3 mm [THT]"]

nets:
  N1: Raspberry_Pi_1.3v3, R1.Pin_1
  N2: Raspberry_Pi_1.GPIO4, U3.OUT, R1.Pin_0, LED3.anode
  GND: Raspberry_Pi_1.GND, LED1.anode, U3.GND, U1.GNDT, U1.+_-, LED3.cathode
  N3: Raspberry_Pi_1.GPIO20, LED1.cathode, U1.FUTURE
  N4: Raspberry_Pi_1.GPIO16, U1.RES
  N5: Raspberry_Pi_1.GPIO15, U1.D0
  5V: Raspberry_Pi_1.5V, U3.VCC, U1.5V
